# Fritzing sketch dark-room (saved by Fritzing 0.9.3b)
breadboards: 1

parts:
  ARDUINO_UNO_R3 = Arduino Uno (Rev3)
  PHOTOCELL = PHOTOCELL [package=photocell]
  R1 = Resistor [tolerance=±10% resistance=10k package=THT]
  R2 = Resistor [tolerance=±5% resistance=220 package=THT]
  LED1 = LED - 5mm [color="Blue (470nm)" package="5 mm [THT]"]

nets:
  N1: ARDUINO_UNO_R3.A0, PHOTOCELL.P$2, R1.Pin_1
  N2: ARDUINO_UNO_R3.D2, R2.Pin_1
  N3: ARDUINO_UNO_R3.5V, PHOTOCELL.P$1
  N4: ARDUINO_UNO_R3.GND, R1.Pin_0, LED1.cathode
  N5: R2.Pin_0, LED1.anode

// code stored in the sketch: dark-room.ino
/**
 * Project Name: DIY Arduino - Project 02: Dark Room
 *
 * File Name: dark_room.ino
 *
 * Description: Automatically turn on the LED when it's dark
 * Find the light switch when you come home from work at night
 *
 * Compatibility: Arduino UNO
 *
 * Phi Luu
 * Portland, Oregon, United States
 * Created December 13, 2015
 * Updated January 15, 2017
 */

// Required hardware I/O connections
const byte photoPin = A0; // connect photocell to A0
const byte ledPin   = 12; // connect LED to 12

// Global constants
const unsigned short photoThres = 100;

void setup() {
    pinMode(ledPin, OUTPUT);
}

void loop() {
    int photoVal = analogRead(photoPin);

    // toggle the light based on the threshold of light
    if (photoVal < photoThres) {
        digitalWrite(ledPin, HIGH);
    } else {
        digitalWrite(ledPin, LOW);
    }
}
