# Fritzing sketch knock-lock (saved by Fritzing 0.9.3b)
breadboards: 1

parts:
  Arduino_UNO = Arduino Uno (Rev3)
  Piezo_Buzzer = Piezo Speaker
  R1 = Resistor [tolerance=±5% resistance=1M package=THT]
  S1 = Pushbutton [package="[SMD]"]
  R2 = Resistor [tolerance=±5% resistance=10k package=THT]
  LED1 = smd LED [color="Red (633nm)" package="0603 [SMD]"]
  LED2 = smd LED [color="Green (555nm)" package="0603 [SMD]"]
  LED3 = smd LED [color="Yellow (585nm)" package="0603 [SMD]"]
  R3 = Resistor [tolerance=±5% resistance=220 package=THT]
  R4 = Resistor [tolerance=±5% resistance=220 package=THT]
  R5 = Resistor [tolerance=±5% resistance=220 package=THT]
  Servo_Motor = Dagu DGServo 9g (Pan and tilt) [part_number=RS001B]
  C1 = Electrolytic Capacitor [capacitance=100µF package="200 mil [THT, electrolytic]"]

nets:
  N1: Arduino_UNO.A0, Piezo_Buzzer.pin1, R1.Pin_0
  N2: Arduino_UNO.D9_PWM, Servo_Motor.pulse
  N3: Arduino_UNO.D2, S1.Pin_1, S1.Pin_2, R2.Pin_0
  N4: Arduino_UNO.D3_PWM, LED3.anode
  N5: Arduino_UNO.D4, LED2.anode
  N6: Arduino_UNO.D5_PWM, LED1.anode
  5V: Arduino_UNO.5V, Piezo_Buzzer.pin2, S1.Pin_3, S1.Pin_4, Servo_Motor.vcc, C1.+
  GND: Arduino_UNO.GND, R1.Pin_1, R2.Pin_1, R3.Pin_1, R4.Pin_1, R5.Pin_1, Servo_Motor.gnd, C1.-
  N7: LED1.cathode, R3.Pin_0
  N8: LED2.cathode, R4.Pin_0
  N9: LED3.cathode, R5.Pin_0

// code stored in the sketch: knock-lock.ino
//****************************************************************************
//
// Project Name: Arduino Projects Book - Project 12: Knock Lock
//
// File Name: knock-lock.ino
//
// Description: Using the Piezo buzzer to make a secret locking mechanism, in
// order to keep intruders out
//
// Compatibility: Arduino UNO
//
// Phi Luu
// Portland, Oregon, United States
// Created September 06, 2016
// Updated September 06, 2016
//
//****************************************************************************

#include <Servo.h>
Servo servoMotor;

// required hardware I/O connections
const byte switchPin = 2;       // switch connected to 2
const byte yellowLEDPin = 3;    // yellow LED connected to ~3
const byte greenLEDPin = 4;     // green LED connnected to 4
const byte redLEDPin = 4;       // red LED connected to ~5
const byte servoPin = 9;        // servo motor connected to ~9
const byte piezoPin = A0;       // piezo buzzer connected to A0

// default baud rate
const unsigned short baudRate = 9600;

// default knock meter
const byte quietKnockVal = 10;
const byte loudKnockVal = 100;
const byte maxNumKnock = 5;

byte switchVal;
byte knockVal;
boolean locked = false;
byte numKnocks = 0;

// put setup code here, to run once
void setup() {
    servoMotor.attach(9);       // attach the servo to ~9
    pinMode(switchPin, INPUT);
    pinMode(yellowLEDPin, OUTPUT);
    pinMode(greenLEDPin, OUTPUT);
    pinMode(redLEDPin, OUTPUT);
    Serial.begin(baudRate);
}

// put main code here, to run repeatedly
void loop() {
    if (locked == false) {
        digitalWrite(greenLEDPin, HIGH);
        switchVal = digitalRead(switchPin);
        if (switchVal == HIGH) {
            locked = true;
            digitalWrite(greenLEDPin, LOW);
            digitalWrite(redLEDPin, HIGH);
            servoMotor.write(90);       // rotate the servo 90 degrees to lock
            Serial.println("ACCESS DENIED");
            delay(1000);    // allow time for the servo to completely lock
        }
    }
    else {
        knockVal = analogRead(piezoPin);
        // require maxNumKnock valid knocks
        if (numKnocks < maxNumKnock && knockVal > 0) {
            if (checkForKnock(knockVal) == true) {
                numKnocks++;
            }
            Serial.print("Need ");
            Serial.print(maxNumKnock - numKnocks);
            Serial.print(" more knock(s)");
        }
        if (numKnocks >= maxNumKnock) {
            locked = false;
            myServo.write(0);
            delay(20);
            digitalWrite(greenLEDPin, HIGH);
            digitalWrite(redLEDPin, LOW);
            Serial.pritnln("ACCESS GRANTED");
        }
    }
}

// checks to see if a knock is valid or not
boolean checkForKnock(byte aKnockVal) {
    if (aKnockVal > quietKnockVal && aKnockVal < loudKnockVal) {
        digitalWrite(yellowLEDPin, HIGH);
        delay(50);
        digitalWrite(yellowLEDPin, LOW);
        Serial.print("Valid knock value: ");
        Serial.println(aKnockVal);
        return true;
    }
    else {
        Serial.print("Invalid knock value: ");
        Serial.println(aKnockVal);
        return false;
    }
}
