# Fritzing sketch love-o-meter (saved by Fritzing 0.9.3b)
breadboards: 1

parts:
  ARDUINO_UNO_R3 = Arduino Uno (Rev3)
  TMP36 = TMP36 Temperature Sensor [package="TO92 [THT]"]
  LED1 = LED - 5mm [color="Yellow (585nm)" package="5 mm [THT]"]
  LED2 = LED - 5mm [color="Yellow (585nm)" package="5 mm [THT]"]
  LED3 = LED - 5mm [color="Yellow (585nm)" package="5 mm [THT]"]
  R1 = Resistor [tolerance=±5% resistance=220 package=THT]
  R2 = Resistor [tolerance=±5% resistance=220 package=THT]
  R3 = Resistor [tolerance=±5% resistance=220 package=THT]

nets:
  N1: ARDUINO_UNO_R3.A0, TMP36.Vout
  GND: ARDUINO_UNO_R3.GND, TMP36.GND, R1.Pin_0, R2.Pin_0, R3.Pin_0
  N2: ARDUINO_UNO_R3.D2, LED3.anode
  N3: ARDUINO_UNO_R3.D3_PWM, LED2.anode
  N4: ARDUINO_UNO_R3.D4, LED1.anode
  N5: ARDUINO_UNO_R3.5V, TMP36.+Vs
  N6: LED1.cathode, R1.Pin_1
  N7: LED2.cathode, R2.Pin_1
  N8: LED3.cathode, R3.Pin_1

// code stored in the sketch: love-o-meter.ino
/**
 * Project Name: Arduino Projects Book - Project 03: Love-O-Meter
 *
 * File Name: love_o_meter.ino
 *
 * Description: Using the temperature sensor, test how hot you really are!
 *
 * Compatibility: Arduino UNO
 *
 * Phi Luu
 * Portland, Oregon, United States
 * Created September 30, 2015
 * Updated January 15, 2017
 */

// Required hardware I/O connections
const byte sensorPin = A0; // connect TMP sensor to A0
const byte LED1      = 2;  // connect LED 1 to 2
const byte LED2      = 3;  // connect LED 2 to ~3
const byte LED3      = 4;  // connect LED 3 to 4

// Global constants
const float baseLineTemp = 20.0;

// Global variables
unsigned int sensorVal;

void setup() {
    Serial.begin(9600);

    for (byte pinNumber = LED1; pinNumber <= LED3; pinNumber++) {
        pinMode(pinNumber, OUTPUT);
        digitalWrite(pinNumber, LOW);
    }
}

void loop() {
    // read & print temperature value
    sensorVal = analogRead(sensorPin);
    Serial.print("Sensor value: ");
    Serial.println(sensorVal);

    // map & print temperature value to voltage
    float voltage = (sensorVal / 1024.0) * 5.0;
    Serial.print("Volts: ");
    Serial.println(voltage);

    // from voltage, define temperature
    float temperature = (voltage - 0.5) * 100;
    Serial.print("Degrees C: ");
    Serial.println(temperature);
    Serial.println();

    // from temperature, indicate the LEDs
    if ((temperature >= baseLineTemp)
            && (temperature < baseLineTemp + 2)) {
        digitalWrite(LED1, HIGH);
        digitalWrite(LED2, HIGH); // level 1: all LEDs turned on
        digitalWrite(LED3, HIGH);
    } else if (temperature < baseLineTemp) {
        digitalWrite(LED1, LOW);
        digitalWrite(LED2, LOW); // level 0: all LEDs turned off
        digitalWrite(LED3, LOW);
    } else if ((temperature >= baseLineTemp + 2)
               && (temperature < baseLineTemp + 4)) {
        digitalWrite(LED1, HIGH);
        digitalWrite(LED2, LOW); // level 2: LED1 turned on, LEDs 2 & 3 turned off
        digitalWrite(LED3, LOW);
    } else if ((temperature >= baseLineTemp + 4)
               && (temperature < baseLineTemp + 6)) {
        digitalWrite(LED1, LOW);
        digitalWrite(LED2, HIGH); // level 3: LED2 turned on, LEDs 1 & 3 turned off
        digitalWrite(LED3, LOW);
    } else {
        digitalWrite(LED1, LOW);
        digitalWrite(LED2, LOW); // level 4: LED 3 turned on, LEDs 1 & 2 turned off
        digitalWrite(LED3, HIGH);
    }
}
