# Fritzing sketch touchy-feely-lamp (saved by Fritzing 0.9.3b)
breadboards: 1

parts:
  ARDUINO_UNO_R3 = Arduino Uno (Rev3)
  LED = smd LED [color="Blue (470nm)" package="0603 [SMD]"]
  R1 = Resistor [tolerance=±5% resistance=220 package=THT]
  R2 = Resistor [tolerance=±5% resistance=1M package=THT]
  CONDUCTIVE_PIECE = Ceramic Capacitor [capacitance=100nF package="100 mil [THT, multilayer]"]

nets:
  N1: ARDUINO_UNO_R3.D12/MISO, LED.anode
  N2: ARDUINO_UNO_R3.GND, R1.Pin_0
  N3: ARDUINO_UNO_R3.D2, R2.Pin_1, CONDUCTIVE_PIECE.0
  N4: ARDUINO_UNO_R3.D4, R2.Pin_0
  N5: LED.cathode, R1.Pin_1

// code stored in the sketch: touchy-feely-lamp.ino
/**
 * Project Name: Arduino Projects Book - Project 13: Touchy-feely Lamp
 *
 * File Name: touchy-feely-lamp.ino
 *
 * Description: Use the capacitance of your body to turn a LED on/off
 * when you touch a piece of conductive material.
 *
 * Compatibility: Arduino UNO
 *
 * Phi Luu
 * Portland, Oregon, United States
 * Created December 18, 2016
 * Updated January 15, 2017
 */

#include <CapacitiveSensor.h>

// Required hardware I/O connections
const byte receivingPin = 2;  // capacitance receiving pin connected to 2
const byte sendingPin   = 4;  // capacitance sending pin connected to 4
const byte ledPin       = 12; // indicator LED pin connected to 12

// capSensor class
CapacitiveSensor capSensor = CapacitiveSensor(sendingPin, receivingPin);

// Global constants
const int threshold            = 45; // different people may have different values
const unsigned short BAUD_RATE = 9600;

void setup() {
    Serial.begin(BAUD_RATE);
    pinMode(ledPin, OUTPUT);
}

void loop() {
    // read 30 samples at a time
    int sensorValue = capSensor.capacitiveSensor(30);

    Serial.print("Sensor value: ");
    Serial.println(sensorValue);

    // turn on the LED if the capacitance is over the threshold
    if (sensorValue > threshold) {
        digitalWrite(ledPin, HIGH);
    } else {
        digitalWrite(ledPin, LOW);
    }

    // delay helps stabilize the sensor
    delay(10);
}
