# Fritzing sketch zoetrope (saved by Fritzing 0.9.3b)
breadboards: 1

parts:
  ARDUINO_UNO_R3 = Arduino Uno (Rev3)
  POWER = Pushbutton [package="[SMD]"]
  DIRECTION = Pushbutton [package="[SMD]"]
  R1 = Resistor [tolerance=±5% resistance=10k package=THT]
  R2 = Resistor [tolerance=±5% resistance=10k package=THT]
  BATTERY = Battery block 9V
  R3 = Rotary Potentiometer (Small) [maximum_resistance=100kΩ package=THT]
  H_BRIDGE_IC = L293D [package=THT]
  DC_MOTOR = DC Motor

nets:
  N1: ARDUINO_UNO_R3.A0, R3.wiper
  N2: ARDUINO_UNO_R3.D9_PWM, H_BRIDGE_IC.Enable_1
  N3: ARDUINO_UNO_R3.GND, R1.Pin_1, R2.Pin_1, BATTERY.-, R3.leg2, H_BRIDGE_IC.0V
  N4: ARDUINO_UNO_R3.D2, H_BRIDGE_IC.In_2
  N5: ARDUINO_UNO_R3.D3_PWM, H_BRIDGE_IC.In_1
  N6: ARDUINO_UNO_R3.D4, DIRECTION.Pin_3, DIRECTION.Pin_4, R2.Pin_0
  N7: ARDUINO_UNO_R3.D5_PWM, POWER.Pin_3, POWER.Pin_4, R1.Pin_0
  N8: ARDUINO_UNO_R3.5V, POWER.Pin_1, POWER.Pin_2, DIRECTION.Pin_1, DIRECTION.Pin_2, R3.leg1, H_BRIDGE_IC.+V
  N9: BATTERY.+, H_BRIDGE_IC.+Vmotor
  N10: H_BRIDGE_IC.Out_1_(_Controlled_by_Enable_1_), DC_MOTOR.pin_1
  N11: H_BRIDGE_IC.Out_2_(_Controlled_by_Enable_1_), DC_MOTOR.pin_2

// code stored in the sketch: zoetrope.ino
/**
 * Project Name: Arduino Projects Book - Project 10: Zoetrope
 *
 * File Name: zoetrope.ino
 *
 * Description: Control the speed and the direction of the DC motor using
 * two switches and a potentiometer
 *
 * Compatibility: Arduino UNO
 *
 * Phi Luu
 * Portland, Oregon, United States
 * Created August 21, 2016
 * Updated January 15, 2017
 */

// Required hardware I/O connections
const byte potPin      = A0;   // connect potentiometer to A0
const byte icInput1    = 3;    // connect IC Input1 to ~3
const byte icInput2    = 2;    // connect IC Input2 to 2
const byte icEnable1   = 9;    // connect IC Enable1 t ~9
const byte dirSwitch   = 4;    // connect direction switch to 4
const byte stateSwitch = 5;    // connect state switch to ~5

// Global variables
byte stateSwitchVal       = 0; // state switch
byte dirSwitchVal         = 0; // direction switch
byte prevStateSwitchVal   = 0; // previous state switch
byte prevDirSwitchVal     = 0; // previous direction switch
byte motorEnabled         = 0; // whether the motor is on/off
byte motorDirection       = 0; // motor direction
unsigned short motorSpeed = 0;

void setup() {
    pinMode(dirSwitch,   INPUT);
    pinMode(stateSwitch, INPUT);
    pinMode(icInput1,    OUTPUT);
    pinMode(icInput2,    OUTPUT);
    pinMode(icEnable1,   OUTPUT);
}

void loop() {
    stateSwitchVal = digitalRead(stateSwitch);
    delay(1);
    dirSwitchVal = digitalRead(dirSwitch);
    motorSpeed   = analogRead(potPin) / 4;

    // process the on/off state of the motor from the state switch
    if (stateSwitchVal != prevStateSwitchVal) {
        if (stateSwitchVal) {
            motorEnabled = !motorEnabled;
        }
    }

    // process the direction of the motor from the direction switch
    if (dirSwitchVal != prevDirSwitchVal) {
        if (dirSwitchVal) {
            motorDirection = !motorDirection;
        }
    }

    // control the direction of the motor using the IC
    if (motorDirection) {
        digitalWrite(icInput1, LOW);
        digitalWrite(icInput2, HIGH);
    } else {
        digitalWrite(icInput1, HIGH);
        digitalWrite(icInput2, LOW);
    }

    // control the on/off state of the motor using PWM
    if (motorEnabled) {
        analogWrite(icEnable1, motorSpeed);
    } else {
        analogWrite(icEnable1, 0);
    }

    // prep for next inputs
    prevStateSwitchVal = stateSwitchVal;
    prevDirSwitchVal   = dirSwitchVal;
}
